// Logisim project questioin_4.circ as structural Verilog: 1 circuit, main circuit main
module main (
  output output_1,
  output output_2
);

  wire and_1_out, clock_1_out, t_ff_1_q, t_ff_1_qn, t_ff_2_q;

  T_Flip_Flop t_ff_1 (
    .clk(clock_1_out), .T(1'b1), .Q(t_ff_1_q), .Qn(t_ff_1_qn), .reset(and_1_out));  // open: preset, en
  Clock clock_1 (.out(clock_1_out));
  T_Flip_Flop t_ff_2 (.clk(t_ff_1_qn), .T(1'b1), .Q(t_ff_2_q), .reset(and_1_out));  // open: Qn, preset, en
  and and_1 (and_1_out, t_ff_1_q, t_ff_2_q);
  D_Flip_Flop #(.trigger("high")) d_ff_1 (
    .clk(clock_1_out), .D(t_ff_2_q), .Q(output_1));  // open: Qn, preset, en, reset
  D_Flip_Flop #(.trigger("falling")) d_ff_2 (
    .clk(clock_1_out), .D(output_1), .Q(output_2));  // open: Qn, preset, en, reset

  // Notes on the sheet:
  //   for question number 4 output 1 is the x and the output 2 is the y
endmodule
