// Logisim project question1.circ as structural Verilog: 1 circuit, main circuit main
module main (
  input  in_1,
  input  in_2,
  input  in_3,
  input  in_4,
  input  in_5,
  output out_6,
  output out_7,
  output out_8,
  output out_9
);

  wire clock_1_out, multiplexer_1_out, multiplexer_2_out, multiplexer_3_out, multiplexer_5_out,
       multiplexer_6_out, multiplexer_7_out, multiplexer_9_out, multiplexer_10_out, multiplexer_11_out,
       multiplexer_13_out, multiplexer_14_out, multiplexer_15_out;

  Clock clock_1 (.out(clock_1_out));
  Multiplexer #(.enable("false")) multiplexer_1 (
    .in0(multiplexer_1_out), .in1(multiplexer_2_out), .out(multiplexer_1_out), .sel(clock_1_out));
  Multiplexer #(.enable("false")) multiplexer_2 (.in0(in_2), .in1(out_9), .out(multiplexer_2_out), .sel(in_1));
  Multiplexer #(.enable("false")) multiplexer_3 (.in0(1'b1), .in1(1'b0), .out(multiplexer_3_out), .sel(clock_1_out));
  Multiplexer #(.enable("false")) multiplexer_4 (
    .in0(out_6), .in1(multiplexer_1_out), .out(out_6), .sel(multiplexer_3_out));
  Multiplexer #(.enable("false")) multiplexer_5 (.in0(in_3), .in1(out_6), .out(multiplexer_5_out), .sel(in_1));
  Multiplexer #(.enable("false")) multiplexer_6 (
    .in0(multiplexer_6_out), .in1(multiplexer_5_out), .out(multiplexer_6_out), .sel(clock_1_out));
  Multiplexer #(.enable("false")) multiplexer_7 (.in0(1'b1), .in1(1'b0), .out(multiplexer_7_out), .sel(clock_1_out));
  Multiplexer #(.enable("false")) multiplexer_8 (
    .in0(out_7), .in1(multiplexer_6_out), .out(out_7), .sel(multiplexer_7_out));
  Multiplexer #(.enable("false")) multiplexer_9 (.in0(in_4), .in1(out_7), .out(multiplexer_9_out), .sel(in_1));
  Multiplexer #(.enable("false")) multiplexer_10 (
    .in0(multiplexer_10_out), .in1(multiplexer_9_out), .out(multiplexer_10_out), .sel(clock_1_out));
  Multiplexer #(.enable("false")) multiplexer_11 (.in0(1'b1), .in1(1'b0), .out(multiplexer_11_out), .sel(clock_1_out));
  Multiplexer #(.enable("false")) multiplexer_12 (
    .in0(out_8), .in1(multiplexer_10_out), .out(out_8), .sel(multiplexer_11_out));
  Multiplexer #(.enable("false")) multiplexer_13 (.in0(in_5), .in1(out_8), .out(multiplexer_13_out), .sel(in_1));
  Multiplexer #(.enable("false")) multiplexer_14 (
    .in0(multiplexer_14_out), .in1(multiplexer_13_out), .out(multiplexer_14_out), .sel(clock_1_out));
  Multiplexer #(.enable("false")) multiplexer_15 (.in0(1'b1), .in1(1'b0), .out(multiplexer_15_out), .sel(clock_1_out));
  Multiplexer #(.enable("false")) multiplexer_16 (
    .in0(out_9), .in1(multiplexer_14_out), .out(out_9), .sel(multiplexer_15_out));

  // Notes on the sheet:
  //   the select line is 0 then load operation and the select line is 1 then rotate operation
  //   outputs
  //   inputs
endmodule
