// Logisim project question_3.circ as structural Verilog: 1 circuit, main circuit main
module main (
  input  in_1,
  output out_2
);

  wire and_1_out, clock_1_out, d_ff_1_q, t_ff_1_q, t_ff_1_qn, t_ff_2_q, t_ff_2_qn, t_ff_3_q;

  Clock clock_1 (.out(clock_1_out));
  T_Flip_Flop t_ff_1 (
    .clk(clock_1_out), .T(in_1), .Q(t_ff_1_q), .Qn(t_ff_1_qn), .reset(and_1_out));  // open: preset, en
  T_Flip_Flop t_ff_2 (.clk(t_ff_1_qn), .T(in_1), .Q(t_ff_2_q), .Qn(t_ff_2_qn), .reset(and_1_out));  // open: preset, en
  T_Flip_Flop t_ff_3 (.clk(t_ff_2_qn), .T(in_1), .Q(t_ff_3_q), .reset(and_1_out));  // open: Qn, preset, en
  and and_1 (and_1_out, t_ff_1_q, t_ff_2_q, t_ff_3_q);
  D_Flip_Flop #(.trigger("falling")) d_ff_1 (
    .clk(clock_1_out), .D(t_ff_3_q), .Q(d_ff_1_q));  // open: Qn, preset, en, reset
  or or_1 (out_2, d_ff_1_q, t_ff_3_q);

  // Notes on the sheet:
  //   for the frequency f/7
endmodule
